// Logisim project project-1.circ as structural Verilog: 2 circuits, main circuit main
module main (
);

  ALU_32 alu_32_1 ();  // open: A, B, out, func
endmodule

module ALU_32 (
  input  [2:0] func,
  input  [31:0] A,
  input  [31:0] B,
  input  [31:0] out
);

  wire [31:0] adder_1_out, adder_2_out, and_1_out, multiplier_1_out, or_1_out, shifter_1_out, shifter_2_out,
       subtractor_1_out;

  Adder #(.width(32)) adder_1 (.a(A), .b(B), .out(adder_1_out));  // open: cin, cout
  Adder #(.width(32)) adder_2 (.a(A), .b(32'h1), .out(adder_2_out));  // open: cin, cout
  Subtractor #(.width(32)) subtractor_1 (.a(A), .b(B), .out(subtractor_1_out));  // open: bin, bout
  Multiplier #(.width(32)) multiplier_1 (.a(A), .b(B), .out(multiplier_1_out));  // open: cin, cout
  Shifter #(.width(32)) shifter_1 (.in(A), .\dist (B[4:0]), .out(shifter_1_out));
  Shifter #(.width(32), .shift("lr")) shifter_2 (.in(A), .\dist (B[4:0]), .out(shifter_2_out));
  assign and_1_out = A & B;  // AND_Gate and_1, 32 bits wide
  assign or_1_out = A | B;  // OR_Gate or_1, 32 bits wide
  Multiplexer #(.select(3), .width(32), .enable("false")) multiplexer_1 (
    .in0(adder_1_out), .in1(adder_2_out), .in2(subtractor_1_out), .in3(multiplier_1_out),
    .in4(shifter_1_out), .in5(shifter_2_out), .in6(and_1_out), .in7(or_1_out), .out(out), .sel(func));

  // Notes on the sheet:
  //   Adder-32
  //   A + 1
  //   A - B
  //   Mult
  //   Shift Left
  //   Shift Right
  //   AND-32
  //   OR-32
endmodule
