// Logisim project prj-3.circ as structural Verilog: 6 circuits, main circuit main
module main (
  output [31:0] out_1
);

  wire Clock, Clr;
  wire [3:0] D_Read_1, D_Read_2, Dest_Reg, fetch_buffer_1_rd_out, fetch_buffer_1_rs_b_out, multiplexer_3_out;
  wire [5:0] fetch_buffer_1_opcode_out;
  wire [15:0] fetch_buffer_1_offset_out;
  wire [31:0] BEQ_PC, bit_extender_1_out, D_Out_1, D_Out_2, dual_ported_register_file_1_out1,
       dual_ported_register_file_1_out2, fetch_buffer_1_pc_out, instruction_memory_1_dout, JALR_PC,
       multiplexer_1_out, multiplexer_4_out, multiplexer_5_out, PC_1, pc_1_dout, ToWrite;

  Multiplexer #(.select(2), .width(32)) multiplexer_1 (
    .in0(PC_1), .in1(BEQ_PC), .in2(JALR_PC), .out(multiplexer_1_out), .sel(2'b00));  // open: in3, en
  PC u_pc_1 (.Din(multiplexer_1_out), .Dout(pc_1_dout), .Clk(Clock), .Clear_PC(Clr));
  Counter #(.width(32), .max('hffffffff)) counter_1 (
    .load(1'b0), .count(1'b1), .Q(out_1), .clk(Clock), .clr(Clr));  // open: D, carry
  Clock clock_1 (.out(Clock));
  Button button_1 (.out(Clr));
  _1 u_1_1 (.Din(pc_1_dout), .Dout(PC_1));
  Instruction_Memory instruction_memory_1 (
    .Din(pc_1_dout), .Dout(instruction_memory_1_dout), .Clk(Clock));  // open: Clear_IR
  Fetch_Buffer fetch_buffer_1 (
    .Offset_In(instruction_memory_1_dout[15:0]), .Rs_B_In(instruction_memory_1_dout[15:12]),
    .Rs_A_In(instruction_memory_1_dout[19:16]), .Rd_In(instruction_memory_1_dout[23:20]),
    .OpCode_In(instruction_memory_1_dout[31:26]), .PC_In(PC_1), .Clk_FBuff(Clock),
    .Offset_Out(fetch_buffer_1_offset_out), .Rs_B_Out(fetch_buffer_1_rs_b_out), .Rs_A_Out(D_Read_2),
    .Rd_Out(fetch_buffer_1_rd_out), .Opcode_Out(fetch_buffer_1_opcode_out), .PC_Out(fetch_buffer_1_pc_out));
  assign bit_extender_1_out = {{16{1'b0}}, fetch_buffer_1_offset_out};  // Bit_Extender bit_extender_1
  Multiplexer #(.width(4), .enable("false")) multiplexer_2 (
    .in0(fetch_buffer_1_rs_b_out), .in1(fetch_buffer_1_rd_out), .out(D_Read_1), .sel(1'b0));
  Multiplexer #(.width(4), .enable("false")) multiplexer_3 (
    .in0(D_Read_2), .in1(fetch_buffer_1_rd_out), .out(multiplexer_3_out), .sel(1'b1));
  ROM #(.addrWidth(6)) rom_1 (.addr(fetch_buffer_1_opcode_out));  // open: data, sel
  Dual_Ported_Register_File dual_ported_register_file_1 (
    .CLK(Clock), .WrREGNO(Dest_Reg), .RdREGNO1(D_Read_1), .RdREGNO2(D_Read_2), .INPUT(ToWrite),
    .OUT1(dual_ported_register_file_1_out1), .OUT2(dual_ported_register_file_1_out2));  // open: WrEN
  Multiplexer #(.width(32), .enable("false")) multiplexer_4 (
    .in0(dual_ported_register_file_1_out1), .in1(D_Out_1), .out(multiplexer_4_out), .sel(1'b0));
  Multiplexer #(.width(32), .enable("false")) multiplexer_5 (
    .in0(dual_ported_register_file_1_out2), .in1(D_Out_2), .out(multiplexer_5_out), .sel(1'b0));
  ID_RR_Buffer id_rr_buffer_1 (
    .Offset_In(bit_extender_1_out), .Data_R1_In(multiplexer_4_out), .Data_R2_In(multiplexer_5_out),
    .Dest_In(multiplexer_3_out), .OpCode_In(fetch_buffer_1_opcode_out), .PC_In(fetch_buffer_1_pc_out),
    .Clk_FBuff(Clock));  // open: Offset_Out, Data_R1_Out, Data_R2_Out, Dest_Out, Opcode_Out, PC_Out

  // Notes on the sheet:
  //   FETCH
  //   Counter
  //   Imm B15-B0
  //   Rs_B B15-B12
  //   Rs_A B19-B16
  //   Rd
  //   B23-B20
  //   Unused
  //   B25-B24
  //   Opcode B31-B26
  //   Imm
  //   Rs_B
  //   Rs_A
  //   Rd
  //   OpCode
  //   PC
  //   Sign Extend
  //   ID/RR
  //   Dest
endmodule

module PC (
  input  [31:0] Din,
  input  Clk,
  input  Clear_PC,
  output [31:0] Dout
);

  Register #(.width(32)) PC (.D(Din), .Q(Dout), .clk(Clk), .clr(Clear_PC));  // open: en
endmodule

// I-MEM
module Instruction_Memory (
  input  [31:0] Din,
  input  Clk,
  input  Clear_IR,
  output [31:0] Dout
);

  RAM #(.addrWidth(24), .dataWidth(32)) ram_1 (
    .addr(Din[23:0]), .data(Dout), .clk(Clk), .ld(1'b1), .clr(Clear_IR));  // open: sel
endmodule

module _1 (
  input  [31:0] Din,
  output [31:0] Dout
);

  Adder #(.width(32)) adder_1 (.a(Din), .b(32'h1), .out(Dout));  // open: cin, cout
endmodule

// FETCH\nBUFFER
module Fetch_Buffer (
  input  [15:0] Offset_In,
  input  [3:0] Rs_B_In,
  input  [3:0] Rs_A_In,
  input  [3:0] Rd_In,
  input  [5:0] OpCode_In,
  input  [31:0] PC_In,
  input  Clk_FBuff,
  output [15:0] Offset_Out,
  output [3:0] Rs_B_Out,
  output [3:0] Rs_A_Out,
  output [3:0] Rd_Out,
  output [5:0] Opcode_Out,
  output [31:0] PC_Out
);

  Register #(.width(16)) register_1 (.D(Offset_In), .Q(Offset_Out), .clk(Clk_FBuff));  // open: en, clr
  Register #(.width(4)) register_2 (.D(Rs_B_In), .Q(Rs_B_Out), .clk(Clk_FBuff));  // open: en, clr
  Register #(.width(4)) register_3 (.D(Rs_A_In), .Q(Rs_A_Out), .clk(Clk_FBuff));  // open: en, clr
  Register #(.width(4)) register_4 (.D(Rd_In), .Q(Rd_Out), .clk(Clk_FBuff));  // open: en, clr
  Register #(.width(6)) register_5 (.D(OpCode_In), .Q(Opcode_Out), .clk(Clk_FBuff));  // open: en, clr
  Register #(.width(32)) register_6 (.D(PC_In), .Q(PC_Out), .clk(Clk_FBuff));  // open: en, clr
endmodule

// ID/RR\nBUFFER
module ID_RR_Buffer (
  input  [31:0] Offset_In,
  input  [31:0] Data_R1_In,
  input  [31:0] Data_R2_In,
  input  [3:0] Dest_In,
  input  [5:0] OpCode_In,
  input  [31:0] PC_In,
  input  Clk_FBuff,
  output [31:0] Offset_Out,
  output [31:0] Data_R1_Out,
  output [31:0] Data_R2_Out,
  output [3:0] Dest_Out,
  output [5:0] Opcode_Out,
  output [31:0] PC_Out
);

  Register #(.width(32)) register_1 (.D(Offset_In), .Q(Offset_Out), .clk(Clk_FBuff));  // open: en, clr
  Register #(.width(32)) register_2 (.D(Data_R1_In), .Q(Data_R1_Out), .clk(Clk_FBuff));  // open: en, clr
  Register #(.width(32)) register_3 (.D(Data_R2_In), .Q(Data_R2_Out), .clk(Clk_FBuff));  // open: en, clr
  Register #(.width(4)) register_4 (.D(Dest_In), .Q(Dest_Out), .clk(Clk_FBuff));  // open: en, clr
  Register #(.width(6)) register_5 (.D(OpCode_In), .Q(Opcode_Out), .clk(Clk_FBuff));  // open: en, clr
  Register #(.width(32)) register_6 (.D(PC_In), .Q(PC_Out), .clk(Clk_FBuff));  // open: en, clr
endmodule
